# Fritzing sketch Chrono (saved by Fritzing 0.9.3b)
breadboards: 1

parts:
  Nokia_5110_LCD_Module1 = Nokia 5110 LCD
  Part1 = Arduino Nano (Rev3.0)
  Start/Stop = Round Pushbutton
  Reset = Round Pushbutton
  C1_2_2µf = Capacitor Polarized [package=cpol-radial-1000uf-63v]
  R1 = Resistor [tolerance=±5% resistance=220 package="0603 [SMD]"]
  Accu_4_2V = Battery Holders [package=lipo-1100mAh]
  On/Off_Switch = Taiway 100-SP-X-T1 SPDT Miniature Toggle Switch [part_number=100-SP-X-T1-0-0-B1-M1 package=THT]

nets:
  GND: Nokia_5110_LCD_Module1.GND, Nokia_5110_LCD_Module1.GND_(out), Part1.GND, Start/Stop.leg0, Reset.leg0, C1_2_2µf.-, Accu_4_2V.-
  N1: Nokia_5110_LCD_Module1.SCLK, Nokia_5110_LCD_Module1.SCLK_(out), Part1.D13/SCK
  N2: Nokia_5110_LCD_Module1.LED, Nokia_5110_LCD_Module1.LED_(out), R1.Pin_0
  N3: Nokia_5110_LCD_Module1.VCC_(out), Part1.3V3
  N4: Nokia_5110_LCD_Module1.SCE_(out), Part1.D10
  N5: Nokia_5110_LCD_Module1.RST_(out), Part1.D8
  N6: Nokia_5110_LCD_Module1.D/C_(out), Part1.D9
  N7: Nokia_5110_LCD_Module1.DN(MODI)_(out), Part1.D11/MOSI
  N8: Part1.D2, Start/Stop.leg1, C1_2_2µf.+
  N9: Part1.D3, R1.Pin_1
  N10: Part1.D4, Reset.leg1
  N11: Part1.VIN, On/Off_Switch.L2
  N12: Accu_4_2V.+, On/Off_Switch.COM

custom parts:
  Nokia 5110 LCD: Nokia 5110 Graphic 84*48 LCD module such as the Sparkfun LCD-10168 or the clones from Ebay. There is example code for the Arduino available from the Sparkfun site in https://learn.sparkfun.com/tutorials/graphic-lcd-hookup-guide This is a 3.3V device, if you are running it from a 5V micro you need a 5V tolorant level translator such as the 74ahc367 to protect the signal imputs. Rafa G. did a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
